# Fritzing sketch Wiring help (saved by Fritzing 0.9.3b)
stripboards: 2

parts:
  Composant1 = Arduino Mega 2560 (Rev3)
  R2 = Rotary Potentiometer (Large) [maximum_resistance=10kΩ package=THT]
  TRS1 = Audio Jack (TRS) 3.5mm [package="PG203J [THT]"]
  TRS2 = Audio Jack (TRS) 3.5mm [package="PG203J [THT]"]
  Composant2 = Arduino Mega 2560 (Rev3)
  Composant3 = Arduino Mega 2560 (Rev3)
  S1 = Square Pushbutton
  LED1 = LED - 5mm [color="Red (633nm)" package="5 mm [THT]"]
  LED2 = LED - 5mm [color="Red (633nm)" package="5 mm [THT]"]
  R4 = Resistor [tolerance=±5% resistance=220 package=THT]
  R3 = Resistor [tolerance=±5% resistance=220 package=THT]
  R5 = Rotary Potentiometer (Large) [maximum_resistance=10kΩ package=THT]
  S2 = Square Pushbutton

nets:
  N1: Composant1.A0, R2.wiper
  N2: Composant1.A1, R5.wiper
  N3: Composant1.D19/RX1, Composant2.D1_TX0
  N4: Composant1.D18/TX1, Composant2.D0_RX0
  GND: Composant1.GND, R2.leg2, Composant2.GND, Composant3.GND, S1.leg1, R4.Pin_1, R3.Pin_1, R5.leg2, S2.leg1
  5V: Composant1.5V, R2.leg1, Composant2.VIN, R5.leg1
  N5: Composant1.D2_PWM, LED1.anode
  N6: Composant1.D4_PWM, LED2.anode
  N7: Composant1.D22, S1.leg0
  N8: Composant1.D24, S2.leg0
  N9: Composant1.D27, TRS2.Tip
  N10: Composant1.D37, TRS1.Tip
  N11: Composant2.D19/RX1, Composant3.D1_TX0
  N12: Composant2.D18/TX1, Composant3.D0_RX0
  5V_2: Composant2.5V, Composant3.VIN
  N13: LED1.cathode, R3.Pin_0
  N14: LED2.cathode, R4.Pin_0

notes:
  GND Bus
  +5V Bus
